# Fritzing sketch 线路图 (saved by Fritzing 0.9.3b)
breadboards: 1

parts:
  元件1 = Arduino Uno (Rev3)
  U6 = 7-SEGMENT-4DIGIT [package=7-segment-4digit]
  R1 = Resistor [tolerance=±5% resistance=220 package=THT]
  R2 = Resistor [tolerance=±5% resistance=220 package=THT]
  R3 = Resistor [tolerance=±5% resistance=220 package=THT]
  R4 = Resistor [tolerance=±5% resistance=220 package=THT]
  BAT1 = Battery Holders [package=battery-aa-kit]

nets:
  N1: 元件1.A2, BAT1.+
  N2: 元件1.D8, U6.6
  N3: 元件1.D9_PWM, U6.3
  N4: 元件1.D10_PWM/SS, R1.Pin_0
  N5: 元件1.D11_PWM/MOSI, R4.Pin_0
  N6: 元件1.D12/MISO, R3.Pin_0
  N7: 元件1.D13/SCK, R2.Pin_0
  N8: 元件1.D2, U6.15
  N9: 元件1.D3_PWM, U6.9
  N10: 元件1.D4, U6.4
  N11: 元件1.D5_PWM, U6.2
  N12: 元件1.D6_PWM, U6.1
  N13: 元件1.D7, U6.14
  N14: 元件1.GND, BAT1.-
  N15: U6.8, R2.Pin_1
  N16: U6.11, R3.Pin_1
  N17: U6.13, R1.Pin_1
  N18: U6.16, R4.Pin_1
