# Fritzing sketch Untitled Sketch (saved by Fritzing 0.9.3b)
breadboards: 1

parts:
  元件1 = Arduino Uno (Rev3)
  元件2 = Arduino Uno (Rev3)
  R2 = Rotary Potentiometer (Small) [maximum_resistance=100kΩ package=THT]
  LED1 = 7-SEGMENT-4DIGIT-YOUNGSUN [package=7-segment-4digit-youngsun]
  R3 = Resistor [tolerance=±5% resistance=300 package="0603 [SMD]"]
  R4 = Resistor [tolerance=±5% resistance=300 package="0603 [SMD]"]
  R5 = Resistor [tolerance=±5% resistance=300 package="0603 [SMD]"]
  R6 = Resistor [tolerance=±5% resistance=300 package="0603 [SMD]"]

nets:
  N1: 元件1.A0, R2.wiper
  GND: 元件1.GND, 元件2.GND, R2.leg1
  N2: 元件1.D0/RX, 元件2.D1/TX
  N3: 元件1.D1/TX, 元件2.D0/RX
  N4: 元件1.5V, R2.leg2
  N5: 元件2.D8, LED1.G
  N6: 元件2.D9_PWM, LED1.DP
  N7: 元件2.D10_PWM/SS, R3.Pin_1
  N8: 元件2.D11_PWM/MOSI, R6.Pin_1
  N9: 元件2.D12/MISO, R5.Pin_1
  N10: 元件2.D13/SCK, R4.Pin_1
  N11: 元件2.D2, LED1.A
  N12: 元件2.D3_PWM, LED1.B
  N13: 元件2.D4, LED1.C
  N14: 元件2.D5_PWM, LED1.D
  N15: 元件2.D6_PWM, LED1.E
  N16: 元件2.D7, LED1.F
  N17: LED1.DIG1, R3.Pin_0
  N18: LED1.DIG2, R6.Pin_0
  N19: LED1.DIG3, R5.Pin_0
  N20: LED1.DIG4, R4.Pin_0
  N21: LED1.APOS-C, LED1.COL-C
