# Fritzing sketch 190716 (saved by Fritzing 0.9.3b)
breadboards: 2

parts:
  元件1 = Arduino Uno (Rev3)
  Disp1 = LBT2088AH [part_number=LBT2088AH]
  IC1 = SHIFT REGISTER [package=dil16]
  IC2 = SHIFT REGISTER [package=dil16]
  R1 = Resistor [tolerance=±5% resistance=300 package=THT]
  R2 = Resistor [tolerance=±5% resistance=300 package=THT]
  R3 = Resistor [tolerance=±5% resistance=300 package=THT]
  R4 = Resistor [tolerance=±5% resistance=300 package=THT]
  R5 = Resistor [tolerance=±5% resistance=300 package=THT]
  R6 = Resistor [tolerance=±5% resistance=300 package=THT]
  R7 = Resistor [tolerance=±5% resistance=300 package=THT]
  R8 = Resistor [tolerance=±5% resistance=300 package=THT]
  U1 = BUTTONPAD-4X4 [package=buttonpad-4x4-special]

nets:
  N1: 元件1.A0, U1.G$9_RED
  N2: 元件1.A1, U1.G$9_GND
  N3: 元件1.D8, U1.G$11_GRN
  N4: 元件1.D9_PWM, U1.G$5_SIG1
  N5: 元件1.D10_PWM/SS, U1.G$10_GRN
  N6: 元件1.D11_PWM/MOSI, U1.G$10_GND
  N7: 元件1.D12/MISO, U1.G$10_RED
  N8: 元件1.D13/SCK, U1.G$10_BLU
  N9: 元件1.D2, IC2.RCK
  N10: 元件1.D3_PWM, IC2.SCK
  N11: 元件1.D4, IC2.SER
  N12: 元件1.D5_PWM, IC1.RCK
  N13: 元件1.D6_PWM, IC1.SCK
  N14: 元件1.D7, IC1.SER
  5V: 元件1.5V, IC1.SCL, IC1.VCC
  GND: 元件1.GND, IC1.GND, IC1.G, IC2.GND
  N15: Disp1.pin1, R1.Pin_1
  N16: Disp1.pin2, IC1.QD
  N17: Disp1.pin_3, IC1.QF
  N18: Disp1.pin_4, R4.Pin_1
  N19: Disp1.pin_5, IC1.QA
  N20: Disp1.pin_6, R2.Pin_1
  N21: Disp1.pin_7, IC1.QG
  N22: Disp1.pin_8, IC1.QH
  N23: Disp1.pin_9, R5.Pin_1
  N24: Disp1.pin_10, R7.Pin_1
  N25: Disp1.pin_11, IC1.QB
  N26: Disp1.pin_12, IC1.QC
  N27: Disp1.pin_13, R8.Pin_1
  N28: Disp1.pin_14, IC1.QE
  N29: Disp1.pin_15, R6.Pin_1
  N30: Disp1.pin_16, R3.Pin_1
  N31: IC2.QB, R2.Pin_0
  N32: IC2.QC, R3.Pin_0
  N33: IC2.QD, R4.Pin_0
  N34: IC2.QE, R5.Pin_0
  N35: IC2.QF, R6.Pin_0
  N36: IC2.QG, R7.Pin_0
  N37: IC2.QH, R8.Pin_0
  N38: IC2.SCL, IC2.VCC
  N39: IC2.QA, R1.Pin_0
